# Fritzing sketch RU_06 (saved by Fritzing 0.9.2b)

parts:
  ETH = Arduino Ethernet Shield (Rev3)
  RU05 = Arduino Micro (Rev3)
  Часть3 = Arduino Nano (Rev3.0)
  Часть4 = RFID-RC522-v2
  Часть5 = RFID-RC522-v2
  Часть6 = RFID-RC522-v2
  DLp1 = RELAY [package=relay-t9a]
  PIR2 = PIR sensor
  DLp2 = RELAY [package=relay-t9a]
  DLven = RELAY [package=relay-t9a]
  DLL2 = RELAY [package=relay-t9a]
  DLL1 = RELAY [package=relay-t9a]
  DLL0 = RELAY [package=relay-t9a]
  R7 = Resistor [tolerance=±5% resistance=10k package=THT]
  C4 = Ceramic Capacitor [capacitance=10nF package="100 mil [THT, multilayer]"]
  D8 = Rectifier Diode [part_number=1N4148 package="300 mil [THT]"]
  D9 = Rectifier Diode [part_number=1N4148 package="300 mil [THT]"]
  D10 = Rectifier Diode [part_number=1N4148 package="300 mil [THT]"]
  S2 = Square Pushbutton

nets:
  N1: ETH.ICSP_MISO, RU05.MISO
  N2: ETH.ICSP_SCK, RU05.SCK
  N3: ETH.ICSP_MOSI, RU05.MOSI
  N4: ETH.RESET, RU05.RESET
  N5: ETH.ETH_CS, RU05.D10_PWM/A10
  N6: RU05.D2/SDA, Часть3.A4
  N7: RU05.D3/SCL, Часть3.A5
  N8: RU05.D4_PWM/A6, R7.Pin_1, C4.0, D9.anode, D10.cathode, S2.leg0
  N9: RU05.D5_PWM, C4.1, D8.anode, D9.cathode, S2.leg1
  N10: RU05.D12_PWM/A11, PIR2.SIG
  N11: RU05.A5, DLL0.COIL1
  N12: RU05.A4, DLL1.COIL1
  N13: RU05.A3, DLL2.COIL1
  N14: RU05.A2, DLven.COIL1
  N15: RU05.A1, DLp2.COIL1
  N16: RU05.A0, DLp1.COIL1
  N17: Часть3.D8, Часть6.IRQ
  N18: Часть3.D9, Часть5.IRQ
  N19: Часть3.D10, Часть4.IRQ
  N20: Часть3.D11/MOSI, Часть4.MOSI, Часть5.MOSI, Часть6.MOSI
  N21: Часть3.D12/MISO, Часть4.MISO, Часть5.MISO, Часть6.MISO
  N22: Часть3.D13/SCK, Часть4.SCK, Часть5.SCK, Часть6.SCK
  GND: R7.Pin_0, D10.anode
  5V: D8.cathode

custom parts:
  RFID-RC522-v2: A simple China made RFID-RC522 Reader; do check the pin labels, as this is a MFRC522 based clone.
